// Digital circuit Inc16.dig as structural Verilog
module Inc16 (
  input  [15:0] in,
  output [15:0] out
);

  Add #(.Bits(16)) add_1 (.a(in), .b(16'h1), .c_i(1'b0), .s(out));  // open: c_o
endmodule
